# Fritzing sketch Kamstrup602 (saved by Fritzing 0.9.0b)
breadboards: 1

parts:
  Part1 = Arduino Uno (Rev3)
  R1 = Resistor [tolerance=±5% resistance=10k package=THT]
  R2 = Resistor [tolerance=±5% resistance=1k package=THT]

nets:
  N1: Part1.D5_PWM, R1.Pin_1
  N2: Part1.D6_PWM, R2.Pin_0
  N3: Part1.5V, R1.Pin_0
